# Fritzing sketch Lichtsensor (saved by Fritzing 0.9.3b)
breadboards: 1

parts:
  R1 = Photocell (LDR) [package=THT]
  R2 = Resistor [tolerance=±5% resistance=1k package=THT]
  Bauteil1 = Arduino Mega 2560 (Rev3)

nets:
  N1: R1.pin_0, Bauteil1.5V
  N2: R1.pin_1, R2.Pin_0, Bauteil1.A0
  N3: R2.Pin_1, Bauteil1.GND
